// Logisim project ULA.circ as structural Verilog: 2 circuits, main circuit main
module main (
  input  [7:0] a,
  input  [7:0] b,
  input  [2:0] op,
  output [7:0] out_4
);

  wire [7:0] adder_1_out, and_1_out, and_2_out, and_3_out, and_4_out, and_5_out, and_6_out, and_7_out,
       and_8_out, and_9_out, codificador_1_out_2, codificador_1_out_3, codificador_1_out_4,
       codificador_1_out_5, codificador_1_out_6, codificador_1_out_7, codificador_1_out_8,
       codificador_1_out_9, nand_1_out, nor_1_out, nor_2_out, not_1_out, or_1_out, xor_1_out;

  codificador codificador_1 (
    .a(op), .out_2(codificador_1_out_2), .out_3(codificador_1_out_3), .out_4(codificador_1_out_4),
    .out_5(codificador_1_out_5), .out_6(codificador_1_out_6), .out_7(codificador_1_out_7),
    .out_8(codificador_1_out_8), .out_9(codificador_1_out_9));
  assign and_1_out = b & a;  // AND_Gate and_1, 8 bits wide
  assign or_1_out = a | b;  // OR_Gate or_1, 8 bits wide
  assign not_1_out = ~a;  // NOT_Gate not_1, 8 bits wide
  assign nand_1_out = ~(a & b);  // NAND_Gate nand_1, 8 bits wide
  assign nor_1_out = ~(a | b);  // NOR_Gate nor_1, 8 bits wide
  assign xor_1_out = a ^ b;  // XOR_Gate xor_1, 8 bits wide
  Adder adder_1 (.a(a), .b(b), .out(adder_1_out));  // open: cin, cout
  assign nor_2_out = ~(b | a);  // NOR_Gate nor_2, 8 bits wide
  assign and_2_out = and_1_out & codificador_1_out_2;  // AND_Gate and_2, 8 bits wide
  assign and_3_out = or_1_out & codificador_1_out_3;  // AND_Gate and_3, 8 bits wide
  assign and_4_out = not_1_out & codificador_1_out_4;  // AND_Gate and_4, 8 bits wide
  assign and_5_out = nand_1_out & codificador_1_out_5;  // AND_Gate and_5, 8 bits wide
  assign and_6_out = nor_1_out & codificador_1_out_6;  // AND_Gate and_6, 8 bits wide
  assign and_7_out = xor_1_out & codificador_1_out_7;  // AND_Gate and_7, 8 bits wide
  assign and_8_out = adder_1_out & codificador_1_out_8;  // AND_Gate and_8, 8 bits wide
  assign and_9_out = nor_2_out & codificador_1_out_9;  // AND_Gate and_9, 8 bits wide
  assign out_4 = and_2_out | and_9_out | and_3_out | and_4_out | and_6_out | and_7_out | and_8_out | and_5_out;  // OR_Gate or_2, 8 bits wide
endmodule

module codificador (
  input  [2:0] a,
  output [7:0] out_2,
  output [7:0] out_3,
  output [7:0] out_4,
  output [7:0] out_5,
  output [7:0] out_6,
  output [7:0] out_7,
  output [7:0] out_8,
  output [7:0] out_9
);

  and and_1 (out_2[7], ~a[2], ~a[1], ~a[0]);  // AND_Gate
  and and_2 (out_3[7], ~a[2], ~a[1], a[0]);  // AND_Gate
  and and_3 (out_4[7], ~a[2], a[1], ~a[0]);  // AND_Gate
  and and_4 (out_5[7], ~a[2], a[1], a[0]);  // AND_Gate
  and and_5 (out_6[7], a[2], ~a[1], ~a[0]);  // AND_Gate
  and and_6 (out_7[7], a[2], ~a[1], a[0]);  // AND_Gate
  and and_7 (out_8[7], a[2], a[1], ~a[0]);  // AND_Gate
  and and_8 (out_9[7], a[2], a[1], a[0]);

  assign out_2[6:0] = {7{out_2[7]}};
  assign out_3[6:0] = {7{out_3[7]}};
  assign out_4[6:0] = {7{out_4[7]}};
  assign out_5[6:0] = {7{out_5[7]}};
  assign out_6[6:0] = {7{out_6[7]}};
  assign out_7[6:0] = {7{out_7[7]}};
  assign out_8[6:0] = {7{out_8[7]}};
  assign out_9[6:0] = {7{out_9[7]}};
endmodule
